// Digital circuit arnicompV2.dig as structural Verilog
module arnicompV2 (
  input  CLK,
  input  nPRST,
  output MA0,
  output MA1,
  output MA2,
  output MA3,
  output MA4,
  output MA5,
  output MA6,
  output MA7,
  output MA8,
  output MA9,
  output MA10,
  output MA11,
  output MA12,
  output MA13,
  output MA14,
  output MA15,
  output nMO,
  output MW,
  output D0,
  output D1,
  output D2,
  output D3,
  output D4,
  output D5,
  output D6,
  output D7
);

  wire _7400_1_pin1, _7400_1_pin2, _7400_1_pin6, _7400_1_pin9, _7400_1_pin10, _7400_1_pin11, _7400_2_pin6,
       _7400_2_pin8, _7400_2_pin9, _7404_1_pin2, _7404_1_pin4, _7404_1_pin5, _7404_1_pin9, _7404_1_pin11,
       _7404_1_pin13, _7404_2_pin2, _7404_2_pin4, _7404_2_pin6, _7404_2_pin8, _7404_2_pin10, _7404_2_pin12,
       _7404_4_pin1, _7404_4_pin3, _7404_4_pin5, _7404_4_pin9, _7404_4_pin11, _7404_5_pin3, _7404_5_pin5,
       _7404_5_pin9, _7404_5_pin11, _7408_1_pin1, _7408_1_pin2, _7408_1_pin4, _7408_1_pin5, _7408_1_pin8,
       _7408_1_pin11, _7408_2_pin1, _7408_2_pin2, _7408_2_pin4, _7408_2_pin5, _7408_2_pin8, _7408_2_pin11,
       _7408_3_pin1, _7408_3_pin2, _7408_3_pin4, _7408_3_pin5, _7408_3_pin8, _7408_3_pin12, _7408_4_pin1,
       _7408_4_pin2, _7408_4_pin4, _7408_4_pin5, _7408_4_pin8, _7408_4_pin12, _7408_6_pin1, _7408_6_pin2,
       _7408_6_pin6, _7408_6_pin9, _7408_6_pin10, _7408_8_pin1, _7408_8_pin2, _7408_8_pin4, _7408_8_pin5,
       _7408_8_pin12, _7408_8_pin13, _7408_9_pin1, _7408_9_pin2, _7408_9_pin4, _7408_9_pin5, _7408_9_pin9,
       _7408_9_pin10, _7432_1_pin1, _7432_1_pin2, _7432_1_pin4, _7432_1_pin5, _7432_1_pin8, _7432_1_pin12,
       _7432_1_pin13, _7483_1_pin4, _7483_1_pin7, _7483_1_pin11, _7483_1_pin13, _7483_1_pin14, _7483_1_pin16,
       _7483_2_pin4, _7483_2_pin7, _7483_2_pin11, _7483_2_pin13, _7483_2_pin16, _7485_1_pin6, _7485_2_pin2,
       _7485_2_pin3, _7485_2_pin4, _7485_2_pin5, _7485_2_pin6, _7485_2_pin7, _74138_1_pin1, _74138_1_pin2,
       _74138_1_pin3, _74138_1_pin11, _74161_1_pin3, _74161_1_pin4, _74161_1_pin5, _74161_1_pin6,
       _74161_1_pin10, _74161_1_pin11, _74161_1_pin12, _74161_1_pin13, _74161_1_pin14, _74161_2_pin3,
       _74161_2_pin4, _74161_2_pin5, _74161_2_pin6, _74161_2_pin10, _74161_2_pin11, _74161_2_pin12,
       _74161_2_pin13, _74161_2_pin14, _74161_3_pin3, _74161_3_pin4, _74161_3_pin5, _74161_3_pin6,
       _74161_3_pin10, _74161_3_pin11, _74161_3_pin12, _74161_3_pin13, _74161_3_pin14, _74161_4_pin11,
       _74161_4_pin12, _74161_4_pin13, _74161_4_pin14, _74238_1_pin1, _74238_1_pin2, _74238_1_pin3,
       _74244_1_pin2, _74244_1_pin4, _74244_1_pin6, _74244_1_pin8, _74244_1_pin11, _74244_1_pin13,
       _74244_1_pin15, _74244_1_pin17, _74244_2_pin1, _74244_2_pin2, _74244_2_pin4, _74244_2_pin6,
       _74244_2_pin8, _74244_2_pin11, _74244_2_pin13, _74244_2_pin15, _74244_3_pin2, _74244_3_pin3,
       _74244_3_pin4, _74244_3_pin5, _74244_3_pin6, _74244_3_pin7, _74244_3_pin8, _74244_3_pin9,
       _74244_3_pin11, _74244_3_pin12, _74244_3_pin13, _74244_3_pin14, _74244_3_pin15, _74244_3_pin16,
       _74244_3_pin17, _74244_3_pin18, _74244_4_pin2, _74244_4_pin4, _74244_4_pin6, _74244_4_pin8,
       _74244_4_pin11, _74244_4_pin13, _74244_4_pin15, _74244_4_pin17, _74244_5_pin2, _74244_5_pin4,
       _74244_5_pin6, _74244_5_pin8, _74244_5_pin11, _74244_5_pin13, _74244_5_pin15, _74244_5_pin17,
       _74244_6_pin2, _74244_6_pin4, _74244_6_pin6, _74244_6_pin8, _74244_6_pin11, _74244_6_pin13,
       _74244_6_pin15, _74244_6_pin17, _74374_4_pin2, _74374_4_pin5, _74374_4_pin6, _74374_4_pin9, Acc_pin11,
       ACCW, and_1_out, AW, BW, CE, CF, decoder_1_out_0, decoder_1_out_1, decoder_1_out_2, decoder_1_out_3,
       DW, EF, EIM3, EJMP, Flag_Register_pin11, GF, IM7, INC, isAnd, isArr, isNot, isXor, JMP, LF, MRHW,
       MRLW, MSBRA, nACCO, nAO, nBO, nDO, not_1_out, notconnected_8_out, notconnected_16_out,
       notconnected_35_out, nPCHO, nPCLO, OE, OPS0, OPS1, PRHW, PRLW, Rd_pin11, SC, SF, SN, undriven,
       undriven_2, undriven_3, undriven_4, WE;
  wire [7:0] add_1_s, multiplexer_1_out;

  not not_1 (not_1_out, CLK);
  _7408 _7408_1 (
    .pin1(_7408_1_pin1), .pin2(_7408_1_pin2), .pin4(_7408_1_pin4), .pin5(_7408_1_pin5), .pin7(1'b0),
    .pin8(_7408_1_pin8), .pin9(MRHW), .pin10(CLK), .pin11(_7408_1_pin11), .pin12(CLK), .pin13(MRLW),
    .pin14(1'b1));  // open: pin3, pin6
  // NotConnected on _7408_1_pin1
  _74161 _74161_1 (
    .pin1(nPRST), .pin2(not_1_out), .pin3(_74161_1_pin3), .pin4(_74161_1_pin4), .pin5(_74161_1_pin5),
    .pin6(_74161_1_pin6), .pin7(CE), .pin8(1'b0), .pin9(JMP), .pin10(_74161_1_pin10), .pin11(_74161_1_pin11),
    .pin12(_74161_1_pin12), .pin13(_74161_1_pin13), .pin14(_74161_1_pin14), .pin16(1'b1));  // open: pin15
  // NotConnected on _7408_1_pin2
  _7485 _7485_1 (
    .pin1(1'b0), .pin2(1'b0), .pin3(1'b1), .pin4(1'b0), .pin6(_7485_1_pin6), .pin8(1'b0), .pin9(MA13),
    .pin10(1'b0), .pin11(MA14), .pin12(1'b0), .pin13(1'b0), .pin14(MA15), .pin15(1'b0), .pin16(1'b1));  // open: pin5, pin7
  // NotConnected on _7408_1_pin4
  // NotConnected on _7408_1_pin5
  _7408 _7408_2 (
    .pin1(_7408_2_pin1), .pin2(_7408_2_pin2), .pin4(_7408_2_pin4), .pin5(_7408_2_pin5), .pin7(1'b0),
    .pin8(_7408_2_pin8), .pin9(PRHW), .pin10(CLK), .pin11(_7408_2_pin11), .pin12(CLK), .pin13(PRLW),
    .pin14(1'b1));  // open: pin3, pin6
  // NotConnected on _7408_2_pin2
  // NotConnected on _7408_2_pin1
  Add #(.Bits(8)) add_1 (
    .a({MA7, MA6, MA5, MA4, MA3, MA2, MA1, MA0}), .b({8{1'b0}}), .c_i(1'b1), .s(add_1_s));  // open: c_o
  // NotConnected on _7408_2_pin4
  _74374 _74374_1 (
    .pin1(1'b0), .pin2(MA8), .pin3(D0), .pin4(D1), .pin5(MA9), .pin6(MA10), .pin7(D2), .pin8(D3),
    .pin9(MA11), .pin10(1'b0), .pin11(_7408_1_pin8), .pin12(MA12), .pin13(D4), .pin14(D5), .pin15(MA13),
    .pin16(MA14), .pin17(D6), .pin18(D7), .pin19(MA15), .pin20(1'b1));
  // NotConnected on notconnected_8_out
  _7408 _7408_3 (
    .pin1(_7408_3_pin1), .pin2(_7408_3_pin2), .pin4(_7408_3_pin4), .pin5(_7408_3_pin5), .pin7(1'b0),
    .pin8(_7408_3_pin8), .pin9(CLK), .pin10(AW), .pin12(_7408_3_pin12), .pin13(notconnected_8_out),
    .pin14(1'b1));  // open: pin3, pin6, pin11
  // NotConnected on _7408_3_pin2
  // NotConnected on _7408_3_pin1
  // NotConnected on _7408_2_pin5
  // NotConnected on _7408_3_pin12
  // NotConnected on _7408_3_pin4
  _74161 _74161_2 (
    .pin1(nPRST), .pin2(not_1_out), .pin3(_74161_2_pin3), .pin4(_74161_2_pin4), .pin5(_74161_2_pin5),
    .pin6(_74161_2_pin6), .pin7(CE), .pin8(1'b0), .pin9(JMP), .pin10(_74161_2_pin10), .pin11(_74161_2_pin11),
    .pin12(_74161_2_pin12), .pin13(_74161_2_pin13), .pin14(_74161_2_pin14), .pin15(_74161_1_pin10),
    .pin16(1'b1));
  _7400 _7400_1 (
    .pin1(_7400_1_pin1), .pin2(_7400_1_pin2), .pin4(_7485_1_pin6), .pin5(_7485_1_pin6), .pin6(_7400_1_pin6),
    .pin7(1'b0), .pin9(_7400_1_pin9), .pin10(_7400_1_pin10), .pin11(_7400_1_pin11), .pin12(CLK), .pin13(MW),
    .pin14(1'b1));  // open: pin3, pin8
  // NotConnected on _7400_1_pin1
  // NotConnected on _7408_3_pin5
  // NotConnected on notconnected_16_out
  _7408 _7408_4 (
    .pin1(_7408_4_pin1), .pin2(_7408_4_pin2), .pin4(_7408_4_pin4), .pin5(_7408_4_pin5), .pin7(1'b0),
    .pin8(_7408_4_pin8), .pin9(CLK), .pin10(BW), .pin12(_7408_4_pin12), .pin13(notconnected_16_out),
    .pin14(1'b1));  // open: pin3, pin6, pin11
  // NotConnected on _7408_4_pin2
  // NotConnected on _7408_4_pin1
  _74374 _74374_2 (
    .pin1(1'b0), .pin2(_74161_2_pin3), .pin3(D0), .pin4(D1), .pin5(_74161_2_pin4), .pin6(_74161_2_pin5),
    .pin7(D2), .pin8(D3), .pin9(_74161_2_pin6), .pin10(1'b0), .pin11(_7408_2_pin8), .pin12(_74161_1_pin3),
    .pin13(D4), .pin14(D5), .pin15(_74161_1_pin4), .pin16(_74161_1_pin5), .pin17(D6), .pin18(D7),
    .pin19(_74161_1_pin6), .pin20(1'b1));
  // NotConnected on _7400_1_pin2
  Multiplexer #(.Bits(8)) multiplexer_1 (
    .sel(INC), .in_0({D7, D6, D5, D4, D3, D2, D1, D0}), .in_1(add_1_s), .out(multiplexer_1_out));
  // NotConnected on _7408_4_pin12
  // NotConnected on _7408_4_pin4
  // NotConnected on _7400_1_pin10
  _7432 _7432_1 (
    .pin1(_7432_1_pin1), .pin2(_7432_1_pin2), .pin4(_7432_1_pin4), .pin5(_7432_1_pin5), .pin7(1'b0),
    .pin8(_7432_1_pin8), .pin9(D7), .pin10(MSBRA), .pin12(_7432_1_pin12), .pin13(_7432_1_pin13), .pin14(1'b1));  // open: pin3, pin6, pin11
  // NotConnected on _7432_1_pin1
  // NotConnected on _7408_4_pin5
  // NotConnected on _7400_1_pin9
  // NotConnected on _7432_1_pin13
  // NotConnected on _7432_1_pin12
  // NotConnected on _7432_1_pin2
  program_mem program_mem_1 (
    .nCE(1'b0), .nOE(1'b0), .nWE(1'b1), .VCC(1'b1), .GND(1'b0), .I_O0(_74244_2_pin2), .I_O1(_74244_2_pin4),
    .I_O2(_74244_2_pin6), .I_O3(_74244_2_pin8), .I_O4(_74244_2_pin11), .I_O5(_74244_2_pin13),
    .I_O6(_74244_2_pin15), .I_O7(undriven_4), .A0(_74161_4_pin14), .A1(_74161_4_pin13), .A2(_74161_4_pin12),
    .A3(_74161_4_pin11), .A4(_74161_3_pin14), .A5(_74161_3_pin13), .A6(_74161_3_pin12), .A7(_74161_3_pin11),
    .A8(_74161_2_pin14), .A9(_74161_2_pin13), .A10(_74161_2_pin12), .A11(_74161_2_pin11),
    .A12(_74161_1_pin14), .A13(_74161_1_pin13), .A14(_74161_1_pin12), .A15(_74161_1_pin11));
  _74161 _74161_3 (
    .pin1(nPRST), .pin2(not_1_out), .pin3(_74161_3_pin3), .pin4(_74161_3_pin4), .pin5(_74161_3_pin5),
    .pin6(_74161_3_pin6), .pin7(CE), .pin8(1'b0), .pin9(JMP), .pin10(_74161_3_pin10), .pin11(_74161_3_pin11),
    .pin12(_74161_3_pin12), .pin13(_74161_3_pin13), .pin14(_74161_3_pin14), .pin15(_74161_2_pin10),
    .pin16(1'b1));
  _74374 _74374_3 (
    .pin1(1'b0), .pin2(MA0), .pin3(multiplexer_1_out[0]), .pin4(multiplexer_1_out[1]), .pin5(MA1),
    .pin6(MA2), .pin7(multiplexer_1_out[2]), .pin8(multiplexer_1_out[3]), .pin9(MA3), .pin10(1'b0),
    .pin11(_7408_1_pin11), .pin12(MA4), .pin13(multiplexer_1_out[4]), .pin14(multiplexer_1_out[5]),
    .pin15(MA5), .pin16(MA6), .pin17(multiplexer_1_out[6]), .pin18(multiplexer_1_out[7]), .pin19(MA7),
    .pin20(1'b1));
  // NotConnected on _7432_1_pin4
  // NotConnected on _7432_1_pin5
  // A623308A a623308a_1: pin names not known; wires that end beside it: 1'b1, _7400_1_pin11, MA12, MA7, MA8, MA6, MA9, MA5, MA11, MA4, nMO, MA3, MA10, MA2, _7400_1_pin6, MA1, D7, MA0, D0, D1, D2, 1'b0
  _74374 _74374_4 (
    .pin1(1'b0), .pin2(_74374_4_pin2), .pin3(D0), .pin4(D1), .pin5(_74374_4_pin5), .pin6(_74374_4_pin6),
    .pin7(D2), .pin8(D3), .pin9(_74374_4_pin9), .pin10(1'b0), .pin11(_7408_2_pin11), .pin12(_74161_3_pin3),
    .pin13(D4), .pin14(D5), .pin15(_74161_3_pin4), .pin16(_74161_3_pin5), .pin17(D6), .pin18(D7),
    .pin19(_74161_3_pin6), .pin20(1'b1));
  _74374 _74374_5 (
    .pin1(nAO), .pin2(D0), .pin3(D0), .pin4(D1), .pin5(D1), .pin6(D2), .pin7(D2), .pin8(D3), .pin9(D3),
    .pin10(1'b0), .pin11(_7408_3_pin8), .pin12(D4), .pin13(D4), .pin14(D5), .pin15(D5), .pin16(D6),
    .pin17(D6), .pin18(_7432_1_pin8), .pin19(D7), .pin20(1'b1));
  _74374 _74374_6 (
    .pin1(nBO), .pin2(D0), .pin3(D0), .pin4(D1), .pin5(D1), .pin6(D2), .pin7(D2), .pin8(D3), .pin9(D3),
    .pin10(1'b0), .pin11(_7408_4_pin8), .pin12(D4), .pin13(D4), .pin14(D5), .pin15(D5), .pin16(D6),
    .pin17(D6), .pin18(D7), .pin19(D7), .pin20(1'b1));
  _74161 _74161_4 (
    .pin1(nPRST), .pin2(not_1_out), .pin3(_74374_4_pin2), .pin4(_74374_4_pin5), .pin5(_74374_4_pin6),
    .pin6(_74374_4_pin9), .pin7(CE), .pin8(1'b0), .pin9(JMP), .pin10(1'b1), .pin11(_74161_4_pin11),
    .pin12(_74161_4_pin12), .pin13(_74161_4_pin13), .pin14(_74161_4_pin14), .pin15(_74161_3_pin10),
    .pin16(1'b1));
  Clogic3_28c16 clogic3_28c16_1 (
    .A0(_74244_2_pin2), .A1(_74244_2_pin4), .A2(_74244_2_pin6), .A3(_74244_2_pin8), .A4(_74244_2_pin11),
    .A5(_74244_2_pin13), .A6(_74244_2_pin15), .A7(undriven_4), .A8(1'b0), .A9(1'b0), .A10(1'b0), .nCE(1'b0),
    .nOE(1'b0), .nWE(1'b1), .VCC(1'b1), .GND(1'b0), .I_O0(undriven_2), .I_O1(undriven_3), .I_O2(MSBRA),
    .I_O3(_74138_1_pin1), .I_O4(_74138_1_pin2), .I_O5(_74138_1_pin3), .I_O6(OE), .I_O7(IM7));
  Clogic1_28c16 clogic1_28c16_1 (
    .A0(_74244_2_pin2), .A1(_74244_2_pin4), .A2(_74244_2_pin6), .A3(_74244_2_pin8), .A4(_74244_2_pin11),
    .A5(_74244_2_pin13), .A6(_74244_2_pin15), .A7(undriven_4), .A8(1'b0), .A9(1'b0), .A10(1'b0), .nCE(1'b0),
    .nOE(1'b0), .nWE(1'b1), .VCC(1'b1), .GND(1'b0), .I_O0(undriven), .I_O1(INC), .I_O2(OPS0), .I_O3(OPS1),
    .I_O4(SN), .I_O5(CE), .I_O6(EJMP), .I_O7(SC));
  _74244 _74244_1 (
    .pin1(nDO), .pin2(_74244_1_pin2), .pin3(D7), .pin4(_74244_1_pin4), .pin5(D6), .pin6(_74244_1_pin6),
    .pin7(D5), .pin8(_74244_1_pin8), .pin9(D4), .pin10(1'b0), .pin11(_74244_1_pin11), .pin12(D3),
    .pin13(_74244_1_pin13), .pin14(D2), .pin15(_74244_1_pin15), .pin16(D1), .pin17(_74244_1_pin17),
    .pin18(D0), .pin19(nDO), .pin20(1'b1));
  _7404 _7404_1 (
    .pin1(D6), .pin2(_7404_1_pin2), .pin3(D7), .pin4(_7404_1_pin4), .pin5(_7404_1_pin5), .pin7(1'b0),
    .pin9(_7404_1_pin9), .pin11(_7404_1_pin11), .pin13(_7404_1_pin13), .pin14(1'b1));  // open: pin6, pin8, pin10, pin12
  _74244 _74244_2 (
    .pin1(_74244_2_pin1), .pin2(_74244_2_pin2), .pin3(D7), .pin4(_74244_2_pin4), .pin5(D6),
    .pin6(_74244_2_pin6), .pin7(D5), .pin8(_74244_2_pin8), .pin9(D4), .pin10(1'b0), .pin11(_74244_2_pin11),
    .pin12(D3), .pin13(_74244_2_pin13), .pin14(D2), .pin15(_74244_2_pin15), .pin16(D1), .pin17(1'b0),
    .pin18(D0), .pin19(_74244_2_pin1), .pin20(1'b1));
  _74244 _74244_3 (
    .pin1(isArr), .pin2(_74244_3_pin2), .pin3(_74244_3_pin3), .pin4(_74244_3_pin4), .pin5(_74244_3_pin5),
    .pin6(_74244_3_pin6), .pin7(_74244_3_pin7), .pin8(_74244_3_pin8), .pin9(_74244_3_pin9), .pin10(1'b0),
    .pin11(_74244_3_pin11), .pin12(_74244_3_pin12), .pin13(_74244_3_pin13), .pin14(_74244_3_pin14),
    .pin15(_74244_3_pin15), .pin16(_74244_3_pin16), .pin17(_74244_3_pin17), .pin18(_74244_3_pin18),
    .pin19(isArr), .pin20(1'b1));
  // NotConnected on _7404_1_pin13
  Jlogic_28c16 jlogic_28c16_1 (
    .A0(_74244_2_pin2), .A1(_74244_2_pin4), .A2(_74244_2_pin6), .A3(LF), .A4(GF), .A5(EF), .A6(CF),
    .A7(EJMP), .A8(1'b0), .A9(1'b0), .A10(1'b0), .nCE(1'b0), .nOE(1'b0), .nWE(1'b1), .VCC(1'b1), .GND(1'b0),
    .I_O2(_7404_4_pin1));  // open: I_O0, I_O1, I_O3, I_O4, I_O5, I_O6, I_O7
  // NotConnected on _7404_1_pin11
  // NotConnected on _7404_1_pin5
  _7485 _7485_2 (
    .pin1(_74244_1_pin17), .pin2(_7485_2_pin2), .pin3(_7485_2_pin3), .pin4(_7485_2_pin4),
    .pin5(_7485_2_pin5), .pin6(_7485_2_pin6), .pin7(_7485_2_pin7), .pin8(1'b0), .pin9(_74244_1_pin11),
    .pin10(D4), .pin11(_74244_1_pin13), .pin12(D5), .pin13(D6), .pin14(_74244_1_pin15), .pin15(D7),
    .pin16(1'b1));
  // NotConnected on _7404_1_pin9
  _74244 _74244_4 (
    .pin1(isNot), .pin2(_74244_4_pin2), .pin3(_74244_3_pin3), .pin4(_74244_4_pin4), .pin5(_74244_3_pin5),
    .pin6(_74244_4_pin6), .pin7(_74244_3_pin7), .pin8(_74244_4_pin8), .pin9(_74244_3_pin9), .pin10(1'b0),
    .pin11(_74244_4_pin11), .pin12(_74244_3_pin12), .pin13(_74244_4_pin13), .pin14(_74244_3_pin14),
    .pin15(_74244_4_pin15), .pin16(_74244_3_pin16), .pin17(_74244_4_pin17), .pin18(_74244_3_pin18),
    .pin19(isNot), .pin20(1'b1));
  _74244 _74244_5 (
    .pin1(isAnd), .pin2(_74244_5_pin2), .pin3(_74244_3_pin3), .pin4(_74244_5_pin4), .pin5(_74244_3_pin5),
    .pin6(_74244_5_pin6), .pin7(_74244_3_pin7), .pin8(_74244_5_pin8), .pin9(_74244_3_pin9), .pin10(1'b0),
    .pin11(_74244_5_pin11), .pin12(_74244_3_pin12), .pin13(_74244_5_pin13), .pin14(_74244_3_pin14),
    .pin15(_74244_5_pin15), .pin16(_74244_3_pin16), .pin17(_74244_5_pin17), .pin18(_74244_3_pin18),
    .pin19(isAnd), .pin20(1'b1));
  _74244 _74244_6 (
    .pin1(isXor), .pin2(_74244_6_pin2), .pin3(_74244_3_pin3), .pin4(_74244_6_pin4), .pin5(_74244_3_pin5),
    .pin6(_74244_6_pin6), .pin7(_74244_3_pin7), .pin8(_74244_6_pin8), .pin9(_74244_3_pin9), .pin10(1'b0),
    .pin11(_74244_6_pin11), .pin12(_74244_3_pin12), .pin13(_74244_6_pin13), .pin14(_74244_3_pin14),
    .pin15(_74244_6_pin15), .pin16(_74244_3_pin16), .pin17(_74244_6_pin17), .pin18(_74244_3_pin18),
    .pin19(isXor), .pin20(1'b1));
  _7404 _7404_2 (
    .pin1(D0), .pin2(_7404_2_pin2), .pin3(D1), .pin4(_7404_2_pin4), .pin5(D2), .pin6(_7404_2_pin6),
    .pin7(1'b0), .pin8(_7404_2_pin8), .pin9(D3), .pin10(_7404_2_pin10), .pin11(D4), .pin12(_7404_2_pin12),
    .pin13(D5), .pin14(1'b1));
  _7400 _7400_2 (
    .pin1(IM7), .pin2(IM7), .pin3(_74244_2_pin1), .pin4(EIM3), .pin5(EIM3), .pin6(_7400_2_pin6), .pin7(1'b0),
    .pin8(_7400_2_pin8), .pin9(_7400_2_pin9), .pin10(_7400_2_pin9), .pin11(_7400_2_pin9),
    .pin12(_74244_2_pin6), .pin13(_74244_2_pin11), .pin14(1'b1));
  _74374 Rd (
    .pin1(1'b0), .pin2(_74244_1_pin2), .pin3(D0), .pin4(D1), .pin5(_74244_1_pin4), .pin6(_74244_1_pin6),
    .pin7(D2), .pin8(D3), .pin9(_74244_1_pin8), .pin10(1'b0), .pin11(Rd_pin11), .pin12(_74244_1_pin11),
    .pin13(D4), .pin14(D5), .pin15(_74244_1_pin13), .pin16(_74244_1_pin15), .pin17(D6), .pin18(D7),
    .pin19(_74244_1_pin17), .pin20(1'b1));
  _74374 Acc (
    .pin1(nACCO), .pin2(D0), .pin3(_74244_3_pin18), .pin4(_74244_3_pin16), .pin5(D1), .pin6(D2),
    .pin7(_74244_3_pin14), .pin8(_74244_3_pin12), .pin9(D3), .pin10(1'b0), .pin11(Acc_pin11), .pin12(D4),
    .pin13(_74244_3_pin9), .pin14(_74244_3_pin7), .pin15(D5), .pin16(D6), .pin17(_74244_3_pin5),
    .pin18(_74244_3_pin3), .pin19(D7), .pin20(1'b1));
  Decoder #(.Selector_Bits(2)) decoder_1 (
    .sel({OPS1, OPS0}), .out_0(decoder_1_out_0), .out_1(decoder_1_out_1), .out_2(decoder_1_out_2),
    .out_3(decoder_1_out_3));
  not not_2 (isArr, decoder_1_out_0);
  not not_3 (isAnd, decoder_1_out_1);
  not not_4 (isXor, decoder_1_out_2);
  not not_5 (isNot, decoder_1_out_3);
  _7485 _7485_3 (
    .pin1(_74244_1_pin8), .pin2(1'b0), .pin3(1'b1), .pin4(1'b0), .pin5(_7485_2_pin4), .pin6(_7485_2_pin3),
    .pin7(_7485_2_pin2), .pin8(1'b0), .pin9(_74244_1_pin2), .pin10(D0), .pin11(_74244_1_pin4), .pin12(D1),
    .pin13(D2), .pin14(_74244_1_pin6), .pin15(D3), .pin16(1'b1));
  _7483 _7483_1 (
    .pin1(_74244_1_pin17), .pin2(_74244_3_pin15), .pin3(_74244_1_pin15), .pin4(_7483_1_pin4), .pin5(1'b1),
    .pin6(_74244_3_pin13), .pin7(_7483_1_pin7), .pin8(_74244_1_pin13), .pin9(_74244_3_pin11),
    .pin10(_74244_1_pin11), .pin11(_7483_1_pin11), .pin12(1'b0), .pin13(_7483_1_pin13),
    .pin14(_7483_1_pin14), .pin15(_74244_3_pin17), .pin16(_7483_1_pin16));
  _74138 _74138_1 (
    .pin1(_74138_1_pin1), .pin2(_74138_1_pin2), .pin3(_74138_1_pin3), .pin4(1'b0), .pin5(1'b0), .pin6(OE),
    .pin7(nMO), .pin8(1'b0), .pin9(nPCHO), .pin10(nPCLO), .pin11(_74138_1_pin11), .pin12(nACCO), .pin13(nBO),
    .pin14(nDO), .pin15(nAO), .pin16(1'b1));
  Clogic2_28c16 clogic2_28c16_1 (
    .A0(_74244_2_pin2), .A1(_74244_2_pin4), .A2(_74244_2_pin6), .A3(_74244_2_pin8), .A4(_74244_2_pin11),
    .A5(_74244_2_pin13), .A6(_74244_2_pin15), .A7(undriven_4), .A8(1'b0), .A9(1'b0), .A10(1'b0), .nCE(1'b0),
    .nOE(1'b0), .nWE(1'b1), .VCC(1'b1), .GND(1'b0), .I_O1(WE), .I_O2(ACCW), .I_O3(_74238_1_pin1),
    .I_O4(_74238_1_pin2), .I_O5(_74238_1_pin3), .I_O6(SF), .I_O7(EIM3));  // open: I_O0
  _74374 Flag_Register (
    .pin1(1'b0), .pin3(1'b0), .pin4(1'b0), .pin7(1'b0), .pin8(1'b0), .pin10(1'b0),
    .pin11(Flag_Register_pin11), .pin12(CF), .pin13(_7483_1_pin14), .pin14(_7485_2_pin5), .pin15(GF),
    .pin16(EF), .pin17(_7485_2_pin6), .pin18(_7485_2_pin7), .pin19(LF), .pin20(1'b1));  // open: pin2, pin5, pin6, pin9
  _74257 _74257_1 (
    .pin1(SN), .pin2(D4), .pin3(_7404_2_pin10), .pin4(_7483_1_pin11), .pin5(D5), .pin6(_7404_2_pin12),
    .pin7(_7483_1_pin7), .pin8(1'b0), .pin9(_7483_1_pin4), .pin10(_7404_1_pin2), .pin11(D6),
    .pin12(_7483_1_pin16), .pin13(_7404_1_pin4), .pin14(D7), .pin15(1'b0), .pin16(1'b1));
  _7404 _7404_3 (
    .pin1(D0), .pin2(_74244_4_pin2), .pin3(D1), .pin4(_74244_4_pin4), .pin5(D2), .pin6(_74244_4_pin6),
    .pin7(1'b0), .pin8(_74244_4_pin15), .pin9(D6), .pin10(_74244_4_pin13), .pin11(D5),
    .pin12(_74244_4_pin11), .pin13(D4), .pin14(1'b1));
  _7408 _7408_5 (
    .pin1(D3), .pin2(_74244_1_pin8), .pin3(_74244_5_pin8), .pin4(D2), .pin5(_74244_1_pin6),
    .pin6(_74244_5_pin6), .pin7(1'b0), .pin8(_74244_5_pin15), .pin9(_74244_1_pin15), .pin10(D6),
    .pin11(_74244_5_pin17), .pin12(_74244_1_pin17), .pin13(D7), .pin14(1'b1));
  _7486 _7486_1 (
    .pin1(D3), .pin2(_74244_1_pin8), .pin3(_74244_6_pin8), .pin4(D2), .pin5(_74244_1_pin6),
    .pin6(_74244_6_pin6), .pin7(1'b0), .pin8(_74244_6_pin15), .pin9(_74244_1_pin15), .pin10(D6),
    .pin11(_74244_6_pin17), .pin12(_74244_1_pin17), .pin13(D7), .pin14(1'b1));
  // NotConnected on notconnected_35_out
  _7404 _7404_4 (
    .pin1(_7404_4_pin1), .pin2(JMP), .pin3(_7404_4_pin3), .pin5(_7404_4_pin5), .pin7(1'b0),
    .pin9(_7404_4_pin9), .pin11(_7404_4_pin11), .pin13(notconnected_35_out), .pin14(1'b1));  // open: pin4, pin6, pin8, pin10, pin12
  // NotConnected on _7404_4_pin11
  // NotConnected on _7404_4_pin3
  _74244 _74244_7 (
    .pin1(_7400_2_pin6), .pin2(_74244_2_pin2), .pin3(D7), .pin4(_74244_2_pin4), .pin5(D6),
    .pin6(_7400_2_pin8), .pin7(D5), .pin8(1'b0), .pin9(D4), .pin10(1'b0), .pin11(1'b0), .pin12(D3),
    .pin13(1'b0), .pin14(D2), .pin15(1'b0), .pin16(D1), .pin17(1'b0), .pin18(D0), .pin19(_7400_2_pin6),
    .pin20(1'b1));
  // NotConnected on _7404_4_pin9
  // NotConnected on _7404_4_pin5
  _7408 _7408_6 (
    .pin1(_7408_6_pin1), .pin2(_7408_6_pin2), .pin4(ACCW), .pin5(CLK), .pin6(_7408_6_pin6), .pin7(1'b0),
    .pin9(_7408_6_pin9), .pin10(_7408_6_pin10), .pin11(Rd_pin11), .pin12(CLK), .pin13(DW), .pin14(1'b1));  // open: pin3, pin8
  // NotConnected on _7408_6_pin1
  // NotConnected on _7408_6_pin2
  _7483 _7483_2 (
    .pin1(_74244_1_pin8), .pin2(_74244_3_pin6), .pin3(_74244_1_pin6), .pin4(_7483_2_pin4), .pin5(1'b1),
    .pin6(_74244_3_pin4), .pin7(_7483_2_pin7), .pin8(_74244_1_pin4), .pin9(_74244_3_pin2),
    .pin10(_74244_1_pin2), .pin11(_7483_2_pin11), .pin12(1'b0), .pin13(_7483_2_pin13), .pin14(_7483_1_pin13),
    .pin15(_74244_3_pin8), .pin16(_7483_2_pin16));
  _7404 _7404_5 (
    .pin1(D3), .pin2(_74244_4_pin8), .pin3(_7404_5_pin3), .pin5(_7404_5_pin5), .pin7(1'b0),
    .pin9(_7404_5_pin9), .pin11(_7404_5_pin11), .pin12(_74244_4_pin17), .pin13(D7), .pin14(1'b1));  // open: pin4, pin6, pin8, pin10
  _7408 _7408_7 (
    .pin1(D1), .pin2(_74244_1_pin4), .pin3(_74244_5_pin4), .pin4(D0), .pin5(_74244_1_pin2),
    .pin6(_74244_5_pin2), .pin7(1'b0), .pin8(_74244_5_pin11), .pin9(_74244_1_pin11), .pin10(D4),
    .pin11(_74244_5_pin13), .pin12(_74244_1_pin13), .pin13(D5), .pin14(1'b1));
  _7486 _7486_2 (
    .pin1(D1), .pin2(_74244_1_pin4), .pin3(_74244_6_pin4), .pin4(D0), .pin5(_74244_1_pin2),
    .pin6(_74244_6_pin2), .pin7(1'b0), .pin8(_74244_6_pin11), .pin9(_74244_1_pin11), .pin10(D4),
    .pin11(_74244_6_pin13), .pin12(_74244_1_pin13), .pin13(D5), .pin14(1'b1));
  _7408 _7408_8 (
    .pin1(_7408_8_pin1), .pin2(_7408_8_pin2), .pin4(_7408_8_pin4), .pin5(_7408_8_pin5), .pin7(1'b0),
    .pin8(Acc_pin11), .pin9(CLK), .pin10(ACCW), .pin12(_7408_8_pin12), .pin13(_7408_8_pin13), .pin14(1'b1));  // open: pin3, pin6, pin11
  // NotConnected on _7408_8_pin1
  _74257 _74257_2 (
    .pin1(SN), .pin2(D0), .pin3(_7404_2_pin2), .pin4(_7483_2_pin11), .pin5(D1), .pin6(_7404_2_pin4),
    .pin7(_7483_2_pin7), .pin8(1'b0), .pin9(_7483_2_pin4), .pin10(_7404_2_pin6), .pin11(D2),
    .pin12(_7483_2_pin16), .pin13(_7404_2_pin8), .pin14(D3), .pin15(1'b0), .pin16(1'b1));
  // NotConnected on _7404_5_pin11
  // NotConnected on _7404_5_pin3
  // NotConnected on _7408_8_pin13
  // NotConnected on _7408_8_pin12
  // NotConnected on _7408_8_pin2
  _7408 _7408_9 (
    .pin1(_7408_9_pin1), .pin2(_7408_9_pin2), .pin4(_7408_9_pin4), .pin5(_7408_9_pin5), .pin7(1'b0),
    .pin9(_7408_9_pin9), .pin10(_7408_9_pin10), .pin11(Flag_Register_pin11), .pin12(CLK), .pin13(SF),
    .pin14(1'b1));  // open: pin3, pin6, pin8
  // NotConnected on _7408_9_pin1
  // NotConnected on _7408_6_pin10
  // NotConnected on _7408_6_pin9
  // NotConnected on _7404_5_pin9
  // NotConnected on _7404_5_pin5
  // NotConnected on _7408_8_pin4
  // NotConnected on _7408_8_pin5
  // NotConnected on _7408_9_pin2
  _74238 _74238_1 (
    .pin1(_74238_1_pin1), .pin2(_74238_1_pin2), .pin3(_74238_1_pin3), .pin4(1'b0), .pin5(1'b0), .pin6(WE),
    .pin7(MW), .pin8(1'b0), .pin9(PRHW), .pin10(PRLW), .pin11(MRHW), .pin12(MRLW), .pin13(BW), .pin14(DW),
    .pin15(AW), .pin16(1'b1));
  // NotConnected on _7408_9_pin10
  // NotConnected on _7408_9_pin4
  // NotConnected on _7408_9_pin5
  // NotConnected on _7408_9_pin9
  xor xor_1 (_7483_2_pin13, SN, and_1_out);
  and and_1 (and_1_out, CF, SC);

  // Notes on the sheet:
  //   CLK: Hz: 2147483647
  //   Carry
endmodule
