// Digital circuit asdas.dig as structural Verilog
module asdas (
  input  CLK,
  input  nPRST,
  output MA0,
  output MA1,
  output MA2,
  output MA3,
  output MA4,
  output MA5,
  output MA6,
  output MA7,
  output MA8,
  output MA9,
  output MA10,
  output MA11,
  output MA12,
  output MA13,
  output MA14,
  output MA15,
  output nMO,
  output MW,
  output D0,
  output D1,
  output D2,
  output D3,
  output D4,
  output D5,
  output D6,
  output D7
);

  wire _7400_1_pin1, _7400_1_pin2, _7400_1_pin6, _7400_1_pin9, _7400_1_pin10, _7400_1_pin11, _7400_2_pin6,
       _7400_2_pin8, _7400_2_pin9, _7404_1_pin2, _7404_1_pin4, _7404_1_pin5, _7404_1_pin9, _7404_1_pin11,
       _7404_2_pin2, _7404_2_pin4, _7404_2_pin6, _7404_2_pin8, _7404_2_pin10, _7404_2_pin12, _7404_3_pin1,
       _7404_3_pin3, _7404_3_pin5, _7404_3_pin9, _7404_3_pin11, _7408_1_pin1, _7408_1_pin2, _7408_1_pin4,
       _7408_1_pin5, _7408_1_pin8, _7408_1_pin11, _7408_2_pin1, _7408_2_pin2, _7408_2_pin4, _7408_2_pin5,
       _7408_2_pin8, _7408_2_pin11, _7408_3_pin1, _7408_3_pin2, _7408_3_pin4, _7408_3_pin5, _7408_3_pin8,
       _7408_3_pin12, _7408_3_pin13, _7408_4_pin2, _7408_4_pin3, _7408_4_pin5, _7408_4_pin6, _7408_4_pin8,
       _7408_4_pin9, _7408_4_pin11, _7408_4_pin12, _7408_5_pin3, _7408_5_pin6, _7408_5_pin8, _7408_5_pin11,
       _7408_6_pin1, _7408_6_pin2, _7408_6_pin4, _7408_6_pin5, _7408_6_pin9, _7408_6_pin10, _7408_7_pin1,
       _7408_7_pin2, _7408_7_pin9, _7408_7_pin10, _7432_1_pin1, _7432_1_pin2, _7432_1_pin4, _7432_1_pin5,
       _7432_1_pin9, _7432_1_pin10, _7483_1_pin4, _7483_1_pin7, _7483_1_pin11, _7483_1_pin13, _7483_1_pin14,
       _7483_1_pin16, _7483_2_pin13, _7485_1_pin6, _7485_2_pin2, _7485_2_pin3, _7485_2_pin4, _7485_2_pin5,
       _7485_2_pin6, _7485_2_pin7, _74161_1_pin3, _74161_1_pin4, _74161_1_pin5, _74161_1_pin6,
       _74161_1_pin10, _74161_1_pin11, _74161_1_pin12, _74161_1_pin13, _74161_1_pin14, _74161_2_pin3,
       _74161_2_pin4, _74161_2_pin5, _74161_2_pin6, _74161_2_pin10, _74161_2_pin11, _74161_2_pin12,
       _74161_2_pin13, _74161_2_pin14, _74161_3_pin3, _74161_3_pin4, _74161_3_pin5, _74161_3_pin6,
       _74161_3_pin10, _74161_3_pin11, _74161_3_pin12, _74161_3_pin13, _74161_3_pin14, _74161_4_pin11,
       _74161_4_pin12, _74161_4_pin13, _74161_4_pin14, _74244_2_pin2, _74244_2_pin4, _74244_2_pin6,
       _74244_2_pin8, _74244_3_pin1, _74257_1_pin2, _74257_1_pin5, _74257_1_pin11, _74257_1_pin14,
       _74257_2_pin2, _74257_2_pin5, _74257_2_pin11, _74257_2_pin14, _74257_4_pin4, _74257_4_pin7,
       _74257_4_pin9, _74257_4_pin12, _74374_3_pin2, _74374_3_pin5, _74374_3_pin6, _74374_3_pin9,
       _74374_6_pin11, Acc_pin11, ACCW, AD0, AD1, AD2, AD3, AD4, AD5, AD6, AD7, and_2_out, AW, CE, CF,
       ControlLogic_p12, ControlLogic_p14, ControlLogic_p16, DW, EAW, EF, EIM3, EJMP, Flag_Register_pin11,
       GF, isAnd, JMP, LF, MH, MHW, MLW, MRHW, MRLW, n0O, nACCO, nAO, nDO, nMHO, nMLO, not_1_out, not_2_out,
       notconnected_19_out, notconnected_23_out, nPCHO, nPCLO, OE, PRHW, PRLW, SC, SN, WE;
  wire [4:0] ControlLogic_p4;

  not not_1 (not_1_out, CLK);
  _74244 _74244_1 (
    .pin1(MH), .pin2(1'b0), .pin3(MA11), .pin4(1'b0), .pin5(MA10), .pin6(1'b0), .pin7(MA9), .pin8(1'b0),
    .pin9(MA8), .pin10(1'b0), .pin11(1'b0), .pin12(MA12), .pin13(1'b0), .pin14(MA13), .pin15(1'b0),
    .pin16(MA14), .pin17(1'b0), .pin18(MA15), .pin19(MH), .pin20(1'b1));
  _74161 _74161_1 (
    .pin1(nPRST), .pin2(not_1_out), .pin3(_74161_1_pin3), .pin4(_74161_1_pin4), .pin5(_74161_1_pin5),
    .pin6(_74161_1_pin6), .pin7(CE), .pin8(1'b0), .pin9(JMP), .pin10(_74161_1_pin10), .pin11(_74161_1_pin11),
    .pin12(_74161_1_pin12), .pin13(_74161_1_pin13), .pin14(_74161_1_pin14), .pin16(1'b1));  // open: pin15
  _7485 _7485_1 (
    .pin1(1'b0), .pin2(1'b0), .pin3(1'b1), .pin4(1'b0), .pin6(_7485_1_pin6), .pin8(1'b0), .pin9(MA13),
    .pin10(1'b0), .pin11(MA14), .pin12(1'b0), .pin13(1'b0), .pin14(MA15), .pin15(1'b0), .pin16(1'b1));  // open: pin5, pin7
  _7408 _7408_1 (
    .pin1(_7408_1_pin1), .pin2(_7408_1_pin2), .pin4(_7408_1_pin4), .pin5(_7408_1_pin5), .pin7(1'b0),
    .pin8(_7408_1_pin8), .pin9(PRHW), .pin10(CLK), .pin11(_7408_1_pin11), .pin12(CLK), .pin13(PRLW),
    .pin14(1'b1));  // open: pin3, pin6
  // NotConnected on _7408_1_pin2
  // NotConnected on _7408_1_pin1
  // NotConnected on _7408_1_pin4
  // NotConnected on _7408_1_pin5
  _74161 _74161_2 (
    .pin1(nPRST), .pin2(not_1_out), .pin3(_74161_2_pin3), .pin4(_74161_2_pin4), .pin5(_74161_2_pin5),
    .pin6(_74161_2_pin6), .pin7(CE), .pin8(1'b0), .pin9(JMP), .pin10(_74161_2_pin10), .pin11(_74161_2_pin11),
    .pin12(_74161_2_pin12), .pin13(_74161_2_pin13), .pin14(_74161_2_pin14), .pin15(_74161_1_pin10),
    .pin16(1'b1));
  _7400 _7400_1 (
    .pin1(_7400_1_pin1), .pin2(_7400_1_pin2), .pin4(_7485_1_pin6), .pin5(_7485_1_pin6), .pin6(_7400_1_pin6),
    .pin7(1'b0), .pin9(_7400_1_pin9), .pin10(_7400_1_pin10), .pin11(_7400_1_pin11), .pin12(CLK), .pin13(MW),
    .pin14(1'b1));  // open: pin3, pin8
  // NotConnected on _7400_1_pin1
  _7408 _7408_2 (
    .pin1(_7408_2_pin1), .pin2(_7408_2_pin2), .pin4(_7408_2_pin4), .pin5(_7408_2_pin5), .pin7(1'b0),
    .pin8(_7408_2_pin8), .pin9(MRHW), .pin10(CLK), .pin11(_7408_2_pin11), .pin12(CLK), .pin13(MRLW),
    .pin14(1'b1));  // open: pin3, pin6
  // NotConnected on _7408_2_pin2
  // NotConnected on _7408_2_pin1
  not not_2 (not_2_out, MH);
  _74374 _74374_1 (
    .pin1(1'b0), .pin2(_74161_2_pin3), .pin3(D0), .pin4(D1), .pin5(_74161_2_pin4), .pin6(_74161_2_pin5),
    .pin7(D2), .pin8(D3), .pin9(_74161_2_pin6), .pin10(1'b0), .pin11(_7408_1_pin8), .pin12(_74161_1_pin3),
    .pin13(D4), .pin14(D5), .pin15(_74161_1_pin4), .pin16(_74161_1_pin5), .pin17(D6), .pin18(D7),
    .pin19(_74161_1_pin6), .pin20(1'b1));
  // NotConnected on _7400_1_pin2
  // NotConnected on _7408_2_pin4
  // NotConnected on _7400_1_pin10
  // NotConnected on _7408_2_pin5
  _7408 _7408_3 (
    .pin1(_7408_3_pin1), .pin2(_7408_3_pin2), .pin4(_7408_3_pin4), .pin5(_7408_3_pin5), .pin7(1'b0),
    .pin8(_7408_3_pin8), .pin9(CLK), .pin10(AW), .pin12(_7408_3_pin12), .pin13(_7408_3_pin13), .pin14(1'b1));  // open: pin3, pin6, pin11
  // NotConnected on _7408_3_pin1
  // NotConnected on _7400_1_pin9
  // NotConnected on _7408_3_pin13
  // NotConnected on _7408_3_pin12
  // NotConnected on _7408_3_pin2
  program_mem program_mem_1 (
    .nCE(1'b0), .nOE(1'b0), .nWE(1'b1), .VCC(1'b1), .GND(1'b0), .I_O0(ControlLogic_p16),
    .I_O1(ControlLogic_p14), .I_O2(ControlLogic_p12), .I_O3(ControlLogic_p4[0]), .I_O4(ControlLogic_p4[1]),
    .I_O5(ControlLogic_p4[2]), .I_O6(ControlLogic_p4[3]), .I_O7(ControlLogic_p4[4]), .A0(_74161_4_pin14),
    .A1(_74161_4_pin13), .A2(_74161_4_pin12), .A3(_74161_4_pin11), .A4(_74161_3_pin14), .A5(_74161_3_pin13),
    .A6(_74161_3_pin12), .A7(_74161_3_pin11), .A8(_74161_2_pin14), .A9(_74161_2_pin13), .A10(_74161_2_pin12),
    .A11(_74161_2_pin11), .A12(_74161_1_pin14), .A13(_74161_1_pin13), .A14(_74161_1_pin12),
    .A15(_74161_1_pin11));
  _74161 _74161_3 (
    .pin1(nPRST), .pin2(not_1_out), .pin3(_74161_3_pin3), .pin4(_74161_3_pin4), .pin5(_74161_3_pin5),
    .pin6(_74161_3_pin6), .pin7(CE), .pin8(1'b0), .pin9(JMP), .pin10(_74161_3_pin10), .pin11(_74161_3_pin11),
    .pin12(_74161_3_pin12), .pin13(_74161_3_pin13), .pin14(_74161_3_pin14), .pin15(_74161_2_pin10),
    .pin16(1'b1));
  _74374 _74374_2 (
    .pin1(not_2_out), .pin2(MA8), .pin3(D0), .pin4(D1), .pin5(MA9), .pin6(MA10), .pin7(D2), .pin8(D3),
    .pin9(MA11), .pin10(1'b0), .pin11(_7408_2_pin8), .pin12(MA12), .pin13(D4), .pin14(D5), .pin15(MA13),
    .pin16(MA14), .pin17(D6), .pin18(D7), .pin19(MA15), .pin20(1'b1));
  // NotConnected on _7408_3_pin4
  // NotConnected on _7408_3_pin5
  // A623308A a623308a_1: pin names not known; wires that end beside it: 1'b1, _7400_1_pin11, MA12, MA7, MA8, MA6, MA9, MA5, MA11, MA4, nMO, MA3, MA10, MA2, _7400_1_pin6, MA1, D7, MA0, D0, D1, D2, 1'b0
  _74374 _74374_3 (
    .pin1(1'b0), .pin2(_74374_3_pin2), .pin3(D0), .pin4(D1), .pin5(_74374_3_pin5), .pin6(_74374_3_pin6),
    .pin7(D2), .pin8(D3), .pin9(_74374_3_pin9), .pin10(1'b0), .pin11(_7408_1_pin11), .pin12(_74161_3_pin3),
    .pin13(D4), .pin14(D5), .pin15(_74161_3_pin4), .pin16(_74161_3_pin5), .pin17(D6), .pin18(D7),
    .pin19(_74161_3_pin6), .pin20(1'b1));
  _74374 _74374_4 (
    .pin1(nAO), .pin2(D0), .pin3(D0), .pin4(D1), .pin5(D1), .pin6(D2), .pin7(D2), .pin8(D3), .pin9(D3),
    .pin10(1'b0), .pin11(_7408_3_pin8), .pin12(D4), .pin13(D4), .pin14(D5), .pin15(D5), .pin16(D6),
    .pin17(D6), .pin18(D7), .pin19(D7), .pin20(1'b1));
  _74161 _74161_4 (
    .pin1(nPRST), .pin2(not_1_out), .pin3(_74374_3_pin2), .pin4(_74374_3_pin5), .pin5(_74374_3_pin6),
    .pin6(_74374_3_pin9), .pin7(CE), .pin8(1'b0), .pin9(JMP), .pin10(1'b1), .pin11(_74161_4_pin11),
    .pin12(_74161_4_pin12), .pin13(_74161_4_pin13), .pin14(_74161_4_pin14), .pin15(_74161_3_pin10),
    .pin16(1'b1));
  _74374 _74374_5 (
    .pin1(1'b0), .pin2(MA0), .pin3(D0), .pin4(D1), .pin5(MA1), .pin6(MA2), .pin7(D2), .pin8(D3), .pin9(MA3),
    .pin10(1'b0), .pin11(_7408_2_pin11), .pin12(MA4), .pin13(D4), .pin14(D5), .pin15(MA5), .pin16(MA6),
    .pin17(D6), .pin18(D7), .pin19(MA7), .pin20(1'b1));
  _74374 Acc (
    .pin1(nACCO), .pin2(D0), .pin3(AD0), .pin4(AD1), .pin5(D1), .pin6(D2), .pin7(AD2), .pin8(AD3), .pin9(D3),
    .pin10(1'b0), .pin11(Acc_pin11), .pin12(D4), .pin13(AD4), .pin14(AD5), .pin15(D5), .pin16(D6),
    .pin17(AD6), .pin18(AD7), .pin19(D7), .pin20(1'b1));
  _7408 _7408_4 (
    .pin1(D7), .pin2(_7408_4_pin2), .pin3(_7408_4_pin3), .pin4(D6), .pin5(_7408_4_pin5), .pin6(_7408_4_pin6),
    .pin7(1'b0), .pin8(_7408_4_pin8), .pin9(_7408_4_pin9), .pin10(D4), .pin11(_7408_4_pin11),
    .pin12(_7408_4_pin12), .pin13(D5), .pin14(1'b1));
  // NotConnected on notconnected_19_out
  _7404 _7404_1 (
    .pin1(D6), .pin2(_7404_1_pin2), .pin3(D7), .pin4(_7404_1_pin4), .pin5(_7404_1_pin5), .pin7(1'b0),
    .pin9(_7404_1_pin9), .pin11(_7404_1_pin11), .pin13(notconnected_19_out), .pin14(1'b1));  // open: pin6, pin8, pin10, pin12
  // _28c16 ControlLogic: pin names not known; wires that end beside it: 1'b1, ControlLogic_p4[4], 1'b0, ControlLogic_p4[3], 1'b0, ControlLogic_p4[2], 1'b1, ControlLogic_p4[1], 1'b0, ControlLogic_p4[0], 1'b0, ControlLogic_p12, 1'b0, ControlLogic_p14, SC, ControlLogic_p16, OE, SN, WE, ACCW, CE, 1'b0
  _74244 _74244_2 (
    .pin1(nDO), .pin2(_74244_2_pin2), .pin3(D7), .pin4(_74244_2_pin4), .pin5(D6), .pin6(_74244_2_pin6),
    .pin7(D5), .pin8(_74244_2_pin8), .pin9(D4), .pin10(1'b0), .pin11(_7408_4_pin9), .pin12(D3),
    .pin13(_7408_4_pin12), .pin14(D2), .pin15(_7408_4_pin5), .pin16(D1), .pin17(_7408_4_pin2), .pin18(D0),
    .pin19(nDO), .pin20(1'b1));
  // NotConnected on _7404_1_pin11
  _74244 _74244_3 (
    .pin1(_74244_3_pin1), .pin2(ControlLogic_p16), .pin3(D7), .pin4(ControlLogic_p14), .pin5(D6),
    .pin6(ControlLogic_p12), .pin7(D5), .pin8(ControlLogic_p4[0]), .pin9(D4), .pin10(1'b0),
    .pin11(ControlLogic_p4[1]), .pin12(D3), .pin13(ControlLogic_p4[2]), .pin14(D2),
    .pin15(ControlLogic_p4[3]), .pin16(D1), .pin17(1'b0), .pin18(D0), .pin19(_74244_3_pin1), .pin20(1'b1));
  // NotConnected on _7404_1_pin9
  // NotConnected on _7404_1_pin5
  Comparator #(.Bits(5)) comparator_1 (.a(ControlLogic_p4), .b(5'b00010), .eq(isAnd));  // open: gt, lt
  Jlogic_28c16 jlogic_28c16_1 (
    .A0(ControlLogic_p16), .A1(ControlLogic_p14), .A2(ControlLogic_p12), .A3(LF), .A4(GF), .A5(EF), .A6(CF),
    .A7(EJMP), .A8(1'b0), .A9(1'b0), .A10(1'b0), .nCE(1'b0), .nOE(1'b0), .nWE(1'b1), .VCC(1'b1), .GND(1'b0),
    .I_O2(_7404_3_pin1));  // open: I_O0, I_O1, I_O3, I_O4, I_O5, I_O6, I_O7
  _7485 _7485_2 (
    .pin1(_7408_4_pin2), .pin2(_7485_2_pin2), .pin3(_7485_2_pin3), .pin4(_7485_2_pin4), .pin5(_7485_2_pin5),
    .pin6(_7485_2_pin6), .pin7(_7485_2_pin7), .pin8(1'b0), .pin9(_7408_4_pin9), .pin10(D4),
    .pin11(_7408_4_pin12), .pin12(D5), .pin13(D6), .pin14(_7408_4_pin5), .pin15(D7), .pin16(1'b1));
  _7408 _7408_5 (
    .pin1(D1), .pin2(_74244_2_pin4), .pin3(_7408_5_pin3), .pin4(D2), .pin5(_74244_2_pin6),
    .pin6(_7408_5_pin6), .pin7(1'b0), .pin8(_7408_5_pin8), .pin9(_74244_2_pin8), .pin10(D3),
    .pin11(_7408_5_pin11), .pin12(_74244_2_pin2), .pin13(D0), .pin14(1'b1));
  _7404 _7404_2 (
    .pin1(D0), .pin2(_7404_2_pin2), .pin3(D1), .pin4(_7404_2_pin4), .pin5(D2), .pin6(_7404_2_pin6),
    .pin7(1'b0), .pin8(_7404_2_pin8), .pin9(D3), .pin10(_7404_2_pin10), .pin11(D4), .pin12(_7404_2_pin12),
    .pin13(D5), .pin14(1'b1));
  _74257 _74257_1 (
    .pin1(isAnd), .pin2(_74257_1_pin2), .pin3(_7408_4_pin8), .pin4(AD4), .pin5(_74257_1_pin5),
    .pin6(_7408_4_pin11), .pin7(AD5), .pin8(1'b0), .pin9(AD6), .pin10(_7408_4_pin6), .pin11(_74257_1_pin11),
    .pin12(AD7), .pin13(_7408_4_pin3), .pin14(_74257_1_pin14), .pin15(1'b0), .pin16(1'b1));
  _7400 _7400_2 (
    .pin1(ControlLogic_p4[4]), .pin2(ControlLogic_p4[4]), .pin3(_74244_3_pin1), .pin4(EIM3), .pin5(EIM3),
    .pin6(_7400_2_pin6), .pin7(1'b0), .pin8(_7400_2_pin8), .pin9(_7400_2_pin9), .pin10(_7400_2_pin9),
    .pin11(_7400_2_pin9), .pin12(ControlLogic_p12), .pin13(ControlLogic_p4[1]), .pin14(1'b1));
  _74374 _74374_6 (
    .pin1(1'b0), .pin2(_74244_2_pin2), .pin3(D0), .pin4(D1), .pin5(_74244_2_pin4), .pin6(_74244_2_pin6),
    .pin7(D2), .pin8(D3), .pin9(_74244_2_pin8), .pin10(1'b0), .pin11(_74374_6_pin11), .pin12(_7408_4_pin9),
    .pin13(D4), .pin14(D5), .pin15(_7408_4_pin12), .pin16(_7408_4_pin5), .pin17(D6), .pin18(D7),
    .pin19(_7408_4_pin2), .pin20(1'b1));
  _74238 _74238_1 (
    .pin1(ControlLogic_p4[0]), .pin2(ControlLogic_p4[1]), .pin3(ControlLogic_p4[2]), .pin4(1'b0),
    .pin5(1'b0), .pin6(WE), .pin7(MHW), .pin8(1'b0), .pin9(MLW), .pin10(PRHW), .pin11(PRLW), .pin12(MRHW),
    .pin13(MRLW), .pin14(DW), .pin15(EAW), .pin16(1'b1));
  _7485 _7485_3 (
    .pin1(_74244_2_pin8), .pin2(1'b0), .pin3(1'b1), .pin4(1'b0), .pin5(_7485_2_pin4), .pin6(_7485_2_pin3),
    .pin7(_7485_2_pin2), .pin8(1'b0), .pin9(_74244_2_pin2), .pin10(D0), .pin11(_74244_2_pin4), .pin12(D1),
    .pin13(D2), .pin14(_74244_2_pin6), .pin15(D3), .pin16(1'b1));
  _74257 _74257_2 (
    .pin1(isAnd), .pin2(_74257_2_pin2), .pin3(_7408_5_pin11), .pin4(AD0), .pin5(_74257_2_pin5),
    .pin6(_7408_5_pin3), .pin7(AD1), .pin8(1'b0), .pin9(AD2), .pin10(_7408_5_pin6), .pin11(_74257_2_pin11),
    .pin12(AD3), .pin13(_7408_5_pin8), .pin14(_74257_2_pin14), .pin15(1'b0), .pin16(1'b1));
  _7483 _7483_1 (
    .pin1(_7408_4_pin2), .pin2(_74257_1_pin11), .pin3(_7408_4_pin5), .pin4(_7483_1_pin4), .pin5(1'b1),
    .pin6(_74257_1_pin5), .pin7(_7483_1_pin7), .pin8(_7408_4_pin12), .pin9(_74257_1_pin2),
    .pin10(_7408_4_pin9), .pin11(_7483_1_pin11), .pin12(1'b0), .pin13(_7483_1_pin13), .pin14(_7483_1_pin14),
    .pin15(_74257_1_pin14), .pin16(_7483_1_pin16));
  _74257 _74257_3 (
    .pin1(SN), .pin2(D4), .pin3(_7404_2_pin10), .pin4(_7483_1_pin11), .pin5(D5), .pin6(_7404_2_pin12),
    .pin7(_7483_1_pin7), .pin8(1'b0), .pin9(_7483_1_pin4), .pin10(_7404_1_pin2), .pin11(D6),
    .pin12(_7483_1_pin16), .pin13(_7404_1_pin4), .pin14(D7), .pin15(1'b0), .pin16(1'b1));
  _74374 Flag_Register (
    .pin1(1'b0), .pin3(1'b0), .pin4(1'b0), .pin7(1'b0), .pin8(1'b0), .pin10(1'b0),
    .pin11(Flag_Register_pin11), .pin12(CF), .pin13(_7483_1_pin14), .pin14(_7485_2_pin5), .pin15(GF),
    .pin16(EF), .pin17(_7485_2_pin6), .pin18(_7485_2_pin7), .pin19(LF), .pin20(1'b1));  // open: pin2, pin5, pin6, pin9
  // NotConnected on notconnected_23_out
  _7404 _7404_3 (
    .pin1(_7404_3_pin1), .pin2(JMP), .pin3(_7404_3_pin3), .pin5(_7404_3_pin5), .pin7(1'b0),
    .pin9(_7404_3_pin9), .pin11(_7404_3_pin11), .pin13(notconnected_23_out), .pin14(1'b1));  // open: pin4, pin6, pin8, pin10, pin12
  // NotConnected on _7404_3_pin11
  // NotConnected on _7404_3_pin3
  _74244 _74244_4 (
    .pin1(_7400_2_pin6), .pin2(ControlLogic_p16), .pin3(D7), .pin4(ControlLogic_p14), .pin5(D6),
    .pin6(_7400_2_pin8), .pin7(D5), .pin8(1'b0), .pin9(D4), .pin10(1'b0), .pin11(1'b0), .pin12(D3),
    .pin13(1'b0), .pin14(D2), .pin15(1'b0), .pin16(D1), .pin17(1'b0), .pin18(D0), .pin19(1'b1), .pin20(1'b1));
  // NotConnected on _7404_3_pin9
  // NotConnected on _7404_3_pin5
  _74138 _74138_1 (
    .pin1(ControlLogic_p16), .pin2(ControlLogic_p14), .pin3(ControlLogic_p12), .pin4(1'b0), .pin5(1'b0),
    .pin6(OE), .pin7(nMHO), .pin8(1'b0), .pin9(nMLO), .pin10(nPCHO), .pin11(nPCLO), .pin12(n0O),
    .pin13(nACCO), .pin14(nDO), .pin15(nAO), .pin16(1'b1));
  _74257 _74257_4 (
    .pin1(SN), .pin2(D0), .pin3(_7404_2_pin2), .pin4(_74257_4_pin4), .pin5(D1), .pin6(_7404_2_pin4),
    .pin7(_74257_4_pin7), .pin8(1'b0), .pin9(_74257_4_pin9), .pin10(_7404_2_pin6), .pin11(D2),
    .pin12(_74257_4_pin12), .pin13(_7404_2_pin8), .pin14(D3), .pin15(1'b0), .pin16(1'b1));
  _7408 _7408_6 (
    .pin1(_7408_6_pin1), .pin2(_7408_6_pin2), .pin4(_7408_6_pin4), .pin5(_7408_6_pin5), .pin7(1'b0),
    .pin9(_7408_6_pin9), .pin10(_7408_6_pin10), .pin11(Flag_Register_pin11), .pin12(CLK), .pin13(ACCW),
    .pin14(1'b1));  // open: pin3, pin6, pin8
  // NotConnected on _7408_6_pin1
  _7408 _7408_7 (
    .pin1(_7408_7_pin1), .pin2(_7408_7_pin2), .pin4(ACCW), .pin5(CLK), .pin6(Acc_pin11), .pin7(1'b0),
    .pin9(_7408_7_pin9), .pin10(_7408_7_pin10), .pin11(_74374_6_pin11), .pin12(CLK), .pin13(DW), .pin14(1'b1));  // open: pin3, pin8
  // NotConnected on _7408_7_pin1
  _7483 _7483_2 (
    .pin1(_74244_2_pin8), .pin2(_74257_2_pin11), .pin3(_74244_2_pin6), .pin4(_74257_4_pin9), .pin5(1'b1),
    .pin6(_74257_2_pin5), .pin7(_74257_4_pin7), .pin8(_74244_2_pin4), .pin9(_74257_2_pin2),
    .pin10(_74244_2_pin2), .pin11(_74257_4_pin4), .pin12(1'b0), .pin13(_7483_2_pin13), .pin14(_7483_1_pin13),
    .pin15(_74257_2_pin14), .pin16(_74257_4_pin12));
  _7432 _7432_1 (
    .pin1(_7432_1_pin1), .pin2(_7432_1_pin2), .pin4(_7432_1_pin4), .pin5(_7432_1_pin5), .pin7(1'b0),
    .pin9(_7432_1_pin9), .pin10(_7432_1_pin10), .pin11(AW), .pin12(EAW), .pin13(ControlLogic_p4[4]),
    .pin14(1'b1));  // open: pin3, pin6, pin8
  // NotConnected on _7432_1_pin1
  // NotConnected on _7408_6_pin2
  // NotConnected on _7408_7_pin2
  or or_1 (MW, MLW, MHW);
  // NotConnected on _7432_1_pin2
  // NotConnected on _7408_6_pin10
  // NotConnected on _7408_6_pin4
  // NotConnected on _7408_6_pin5
  // NotConnected on _7408_7_pin10
  and and_1 (nMO, nMLO, nMHO);
  or or_2 (MH, ~nMHO, MHW);  // Or
  // NotConnected on _7432_1_pin10
  // NotConnected on _7432_1_pin4
  // NotConnected on _7432_1_pin5
  // NotConnected on _7408_6_pin9
  // NotConnected on _7408_7_pin9
  xor xor_1 (_7483_2_pin13, SN, and_2_out);
  // NotConnected on _7432_1_pin9
  and and_2 (and_2_out, CF, SC);

  // Notes on the sheet:
  //   CLK: Hz: 2147483647
  //   contents of Program (hex, n*v repeats v):
  //   C:\Users\ssonm\Desktop\projs\ArniComp-Support-Package\assemblerV2_python\examples\last.hex false
endmodule
