// Digital circuit main.dig as structural Verilog
module main (
  input  clk,
  input  in_2
);

  wire a1, a2, a3, and_1_out, and_2_out, b1, b2, b3, c1, c2, c3, comparator_1_eq, comparator_2_eq, d1, d2,
       d3, e1, e2, e3, f1, f2, f3, g1, g2, g3, undriven_2, undriven_3;
  wire [7:0] button_1_out, driver_1_out, register_1_q;
  wire [7:7] rom_1_d, rom_2_d, rom_3_d;
  wire [15:0] undriven;

  arnicompV2 arnicompv2_1 ();
  Button button_1 (.out(button_1_out[7]));
  Button button_2 (.out(button_1_out[6]));
  Button button_3 (.out(button_1_out[5]));
  Button button_4 (.out(button_1_out[4]));
  Button button_5 (.out(button_1_out[3]));
  Button button_6 (.out(button_1_out[2]));
  Button DOWN (.out(button_1_out[1]));
  Button UP (.out(button_1_out[0]));
  Comparator #(.Bits(16)) comparator_1 (.a(undriven), .b(16'h1000), .eq(comparator_1_eq));  // open: gt, lt
  Seven_Seg seven_seg_1 (.a(a3), .b(b3), .c(c3), .d(d3), .e(e3), .f(f3), .g(g3), .dp(1'b0));
  Comparator #(.Bits(16)) comparator_2 (.a(undriven), .b(16'h2000), .eq(comparator_2_eq));  // open: gt, lt
  and and_1 (and_1_out, undriven_2, comparator_1_eq);
  Seven_Seg seven_seg_2 (.a(a2), .b(b2), .c(c2), .d(d2), .e(e2), .f(f2), .g(g2), .dp(1'b0));
  and and_2 (and_2_out, ~undriven_3, comparator_2_eq);  // And
  Seven_Seg seven_seg_3 (.a(a1), .b(b1), .c(c1), .d(d1), .e(e1), .f(f1), .g(g1), .dp(1'b0));
  Register #(.Bits(8)) register_1 (.D(driver_1_out), .C(clk), .en(and_1_out), .Q(register_1_q));
  assign driver_1_out = and_2_out ? button_1_out : 8'bz;  // Driver driver_1
  ROM #(.AddrBits(8), .Bits(8)) rom_1 (.A(register_1_q), .sel(1'b1), .D({rom_1_d[7], g1, f1, e1, d1, c1, b1, a1}));
  ROM #(.AddrBits(8), .Bits(8)) rom_2 (.A(register_1_q), .sel(1'b1), .D({rom_2_d[7], g2, f2, e2, d2, c2, b2, a2}));
  ROM #(.AddrBits(8), .Bits(8)) rom_3 (.A(register_1_q), .sel(1'b1), .D({rom_3_d[7], g3, f3, e3, d3, c3, b3, a3}));

  // Notes on the sheet:
  //   clk: Hz: 100
  //   contents of rom_1 (hex, n*v repeats v):
  //   3f,6,5b,4f,66,6d,7d,7,7f,6f,3f,6,5b,4f,66,6d,7d,7,7f,6f,3f,6,5b
  //   ,4f,66,6d,7d,7,7f,6f,3f,6,5b,4f,66,6d,7d,7,7f,6f,3f,6,5b,4f,66
  //   ,6d,7d,7,7f,6f,3f,6,5b,4f,66,6d,7d,7,7f,6f,3f,6,5b,4f,66,6d,7d
  //   ,7,7f,6f,3f,6,5b,4f,66,6d,7d,7,7f,6f,3f,6,5b,4f,66,6d,7d,7,7f
  //   ,6f,3f,6,5b,4f,66,6d,7d,7,7f,6f,3f,6,5b,4f,66,6d,7d,7,7f,6f,3f
  //   ,6,5b,4f,66,6d,7d,7,7f,6f,3f,6,5b,4f,66,6d,7d,7,7f,6f,3f,6,5b
  //   ,4f,66,6d,7d,7,7f,6f,3f,6,5b,4f,66,6d,7d,7,7f,6f,3f,6,5b,4f,66
  //   ,6d,7d,7,7f,6f,3f,6,5b,4f,66,6d,7d,7,7f,6f,3f,6,5b,4f,66,6d,7d
  //   ,7,7f,6f,3f,6,5b,4f,66,6d,7d,7,7f,6f,3f,6,5b,4f,66,6d,7d,7,7f
  //   ,6f,3f,6,5b,4f,66,6d,7d,7,7f,6f,3f,6,5b,4f,66,6d,7d,7,7f,6f,3f
  //   ,6,5b,4f,66,6d,7d,7,7f,6f,3f,6,5b,4f,66,6d,7d,7,7f,6f,3f,6,5b
  //   ,4f,66,6d,7d,7,7f,6f,3f,6,5b,4f,66,6d
  //   contents of rom_2 (hex, n*v repeats v):
  //   10*0,10*6,10*5b,10*4f,10*66,10*6d,10*7d,10*7,10*7f,10*6f,10*3f
  //   ,10*6,10*5b,10*4f,10*66,10*6d,10*7d,10*7,10*7f,10*6f,10*3f,10*6
  //   ,10*5b,10*4f,10*66,6*6d
  //   contents of rom_3 (hex, n*v repeats v):
  //   100*0,100*6,56*5b
endmodule
