// Digital circuit program_mem.dig as structural Verilog
// 512K-Bit (64K x 8) CMOS Parallel EEPROM;
// DATA Polling for End of Write Detection not implemented!
module program_mem (
  input  nCE,
  input  nOE,
  input  nWE,
  input  VCC,
  input  GND,
  input  I_O0,
  input  I_O1,
  input  I_O2,
  input  I_O3,
  input  I_O4,
  input  I_O5,
  input  I_O6,
  input  I_O7,
  input  A0,
  input  A1,
  input  A2,
  input  A3,
  input  A4,
  input  A5,
  input  A6,
  input  A7,
  input  A8,
  input  A9,
  input  A10,
  input  A11,
  input  A12,
  input  A13,
  input  A14,
  input  A15
);

  wire nor_1_out;
  wire [7:0] Program_d;

  EEPROM #(.AddrBits(16), .isProgramMemory("true"), .Bits(8)) Program (
    .A({A15, A14, A13, A12, A11, A10, A9, A8, A7, A6, A5, A4, A3, A2, A1, A0}), .CS(~nCE), .WE(~nWE),
    .OE(~nOE), .D(Program_d));
  nor nor_1 (nor_1_out, nCE, ~nWE, nOE);  // NOr
  PowerSupply powersupply_1 (.VDD(VCC), .GND(GND));
  BusSplitter #(.Bits(8)) bussplitter_1 (
    .D(Program_d), .OE(nor_1_out), .D0(I_O0), .D1(I_O1), .D2(I_O2), .D3(I_O3), .D4(I_O4), .D5(I_O5),
    .D6(I_O6), .D7(I_O7));

  // Notes on the sheet:
  //   nCE: pin 22, default 1
  //   nOE: pin 24, default 1
  //   nWE: pin 31, default 1
  //   VCC: pin 32, default 1
  //   GND: pin 16
  //   I_O0: pin 13
  //   I_O1: pin 14
  //   I_O2: pin 15
  //   I_O3: pin 17
  //   I_O4: pin 18
  //   I_O5: pin 19
  //   I_O6: pin 20
  //   I_O7: pin 21
  //   A0: pin 12
  //   A1: pin 11
  //   A2: pin 10
  //   A3: pin 9
  //   A4: pin 8
  //   A5: pin 7
  //   A6: pin 6
  //   A7: pin 5
  //   A8: pin 27
  //   A9: pin 26
  //   A10: pin 23
  //   A11: pin 25
  //   A12: pin 4
  //   A13: pin 28
  //   A14: pin 29
  //   A15: pin 3
  //   contents of Program (hex, n*v repeats v):
  //   80,43,47,84,43,80,47,80,43,a0,44,79,3,4f,80,44,79,81,28,3,5f,43
  //   ,79,82,28,3,3,5f,81,41,82,43,6,b9,45,66,80,41,84,43,6,b6,45,66
  //   ,80,43,79,31,5f,81,41,84,43,4f,db,45,60,82,41,83,43,6,d6,45,66
  //   ,80,41,84,43,6,d3,45,66,80,43,79,81,10,5f,41,84,43,4f,db,45,60
  //   ,80,41,84,43,4f,80,43,79,90,44,4f,87,45,60
endmodule
