// Digital circuit screen_control.dig as structural Verilog
module screen_control (
  input  in_1,
  input  in_2,
  input  in_3,
  input  in_4,
  input  [6:0] in_5,
  input  [15:0] ADDR_BASE,
  input  [15:0] ADDR_IN,
  input  clk,
  input  [6:0] in_9
);

  wire comparator_1_eq, comparator_2_eq;
  wire [6:0] add_2_s, register_1_q, register_2_q;
  wire [13:0] mul_1_mul;
  wire [15:0] add_1_s;

  Add #(.Bits(16)) add_1 (.a(ADDR_BASE), .b(16'h1), .c_i(1'b0), .s(add_1_s));  // open: c_o
  Comparator #(.Bits(16)) comparator_1 (.a(ADDR_IN), .b(ADDR_BASE), .eq(comparator_1_eq));  // open: gt, lt
  Comparator #(.Bits(16)) comparator_2 (.a(ADDR_IN), .b(add_1_s), .eq(comparator_2_eq));  // open: gt, lt
  Register #(.Bits(7)) register_1 (.D(in_5), .C(clk), .en(comparator_1_eq), .Q(register_1_q));
  Register #(.Bits(7)) register_2 (.D(in_9), .C(clk), .en(comparator_2_eq), .Q(register_2_q));
  Mul #(.Bits(7)) mul_1 (.a(register_2_q), .b(7'b0001000), .mul(mul_1_mul));
  Add #(.Bits(7)) add_2 (.a(register_1_q), .b(mul_1_mul[6:0]), .c_i(1'b0), .s(add_2_s));  // open: c_o
  GraphicCard #(.graphicHeight(8), .graphicWidth(8)) graphiccard_1 (
    .A(add_2_s), .str(in_1), .C(clk), .ld(in_2), .B(in_3), .D(in_4));
endmodule
